# Fritzing sketch arduino-LED-display-2x7segments (saved by Fritzing 0.8.7b)
breadboards: 1

parts:
  Součástka1 = Arduino Leonardo (Rev3b)
  2_Digit_7_Segment_LED_CC_Display_RED1 = 2 Digit 7 Segment LED CC Display RED
  R1 = Resistor [tolerance=±5% resistance=150 package=THT]
  U1 = SN74LS20N [package="DIP14 [THT]"]
  U2 = SN74LS20N [package="DIP14 [THT]"]

nets:
  VCC: Součástka1.5V, U1.VCC, U2.VCC
  GND: Součástka1.GND, U1.GND, U2.GND
  N1: Součástka1.D9_PWM/A9, U1.2A, U2.2A
  N2: Součástka1.D10_PWM/A10, U1.2Y, U2.2Y
  N3: Součástka1.D11_PWM, U2.1A, U2.1B
  N4: Součástka1.D12/A11, R1.Pin_1
  N5: 2_Digit_7_Segment_LED_CC_Display_RED1.pin12, 2_Digit_7_Segment_LED_CC_Display_RED1.pin13, R1.Pin_0
  N6: U1.1A, U2.2D

custom parts:
  2 Digit 7 Segment LED CC Display RED: 2 digit 7 segment LED display RED
